# Fritzing sketch Central Hub (saved by Fritzing 1.0.6)
breadboards: 1

parts:
  SMA_External_Antenna_via_U_FL_Connector = SMA_Antenna_c97m2
  ESP32-32U = ESP32U
  Micro_SD_Card_5V_Module = Micro SD card reader
  RTC_Module = DS3231_RTC
  OLED_Screen = Grove OLED 128x96
  C1 = Capacitor Polarized [package=cpol-radial-100uf-25v]

nets:
  N1: SMA_External_Antenna_via_U_FL_Connector.connector0, ESP32-32U.ANT
  N2: ESP32-32U.P21, Micro_SD_Card_5V_Module.Pin_6
  N3: ESP32-32U.P23, Micro_SD_Card_5V_Module.Pin_3
  N4: ESP32-32U.P24, RTC_Module.connector3, OLED_Screen.SDA
  N5: ESP32-32U.P25, RTC_Module.connector2, OLED_Screen.SCL
  N6: ESP32-32U.P26, Micro_SD_Card_5V_Module.Pin_5
  N7: ESP32-32U.P27, Micro_SD_Card_5V_Module.Pin_4
  N8: ESP32-32U.P28, Micro_SD_Card_5V_Module.Pin_2
  N9: ESP32-32U.P35, RTC_Module.connector5, OLED_Screen.GND
  N10: ESP32-32U.P36, Micro_SD_Card_5V_Module.Pin_1, RTC_Module.connector4, OLED_Screen.VCC, C1.+
  N11: ESP32-32U.P38, C1.-

notes:
  ESP32-32U is powered by 5V 1A wall adapter

custom parts:
  Micro SD card reader: Micro SD card reader.
