# Fritzing sketch Node (saved by Fritzing 1.0.6)
# 18650 Li-ion Battery: CC-BY Dr Kristofer Chan, King's College London/Remote-research.org
breadboards: 1

parts:
  MCU = DOIT Esp32 DevKit v1 (30 pins long, 11 pins width) [part_number=ESP32S-PIN30]
  3V3_LDO = HT7333-A 3.3V LDO (SOT-89) [part_number=HT7333-A]
  Solar_Panel = SolarPanel_5V_250mW_89fzt
  Temperature_and_Humidity_Sensor = BME280
  TP4056 = TP4056 [chip_label=TP4056 package="DIP (Dual Inline) [THT]"]
  Battery = 18650 Li-ion Battery [package=battery-18650]
  Voltage_Sensor = Voltage Sensor 25V
  Soil_Sensor = DFRobot Capacitive Soil Moisture Sensor V1.0 [part_number=SEN0193]
  C1 = Capacitor Polarized [package=cpol-radial-100uf-25v]
  C2 = Capacitor Polarized [package=cpol-radial-100uf-25v]

nets:
  3V3: MCU.3V3, 3V3_LDO.VOUT, Temperature_and_Humidity_Sensor.VIN, Soil_Sensor.VCC, C2.+
  GND: MCU.GND, 3V3_LDO.GND, Temperature_and_Humidity_Sensor.GND, TP4056.pin6, Voltage_Sensor.GND, Voltage_Sensor.-, Soil_Sensor.GND, C1.-, C2.-
  N1: MCU.D21, Temperature_and_Humidity_Sensor.SDA
  N2: MCU.D22, Temperature_and_Humidity_Sensor.SCL
  N3: MCU.D34, Soil_Sensor.A
  N4: MCU.D35, Voltage_Sensor.S
  VIN: 3V3_LDO.VIN, TP4056.pin3, Voltage_Sensor.VCC, C1.+
  N5: Solar_Panel.connector0, TP4056.pin1
  N6: Solar_Panel.connector1, TP4056.pin2
  N7: TP4056.pin4, Battery.+
  N8: TP4056.pin5, Battery.-

custom parts:
  DOIT Esp32 DevKit v1 (30 pins long, 11 pins width): The DOIT Esp32 DevKit v1 is one of the development board created by DOIT to evaluate the ESP-WROOM-32 module. It is based on the ESP32 microcontroller that boasts Wifi, Bluetooth, Ethernet and Low Power support all in a single chip. (vanepp) made breadboard work, adjusted pin numbering and labels and reduced size of schematic and cleaned up pcb. This chip is 30pins long (2 x15) and 11 pins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
  HT7333-A 3.3V LDO (SOT-89): HT7333-A Low Dropout Linear Regulator 3.3V. Professional schematic view with GND(L), VIN(M), VOUT(R).
  BME280: Temperature Humidity Barometric presure Sensor
  TP4056: A DIP stand-in part for whatever IC you want. With 6 pins on a 300mil dual inline package (DIP) footprint.
  18650 Li-ion Battery: 18650 li-ion Battery Standard 18650 battery with interactive connectors Creative Common Attribution 4.0 International (CC-BY 4.0) license. Any use of this part requires attribution of Dr Kristofer Chan, Department of Geography, King's College London. Contact kristofer.chan [at] kcl.ac.uk OR kris [at] remote-research.org for further information.
  DFRobot Capacitive Soil Moisture Sensor V1.0: DFRobot Capacitive Soil Moisture Sensor V1.0 This product measures soil moisture levels by capacitive sensing, rather than resistive sensing like other types of moisture sensor. It is made of a corrosion resistant material giving it a long service life. Insert it into soil and impress your friends with the real-time soil moisture data! The product includes an on-board voltage regulator which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
